# Fritzing sketch circuit1 (saved by Fritzing 0.9.3b)
breadboards: 1

parts:
  R1 = Resistor [tolerance=±20% resistance=2k package=THT]
  R2 = Resistor [tolerance=±10% resistance=2k package=THT]
  R3 = Resistor [tolerance=±5% resistance=2k package=THT]
  R4 = Resistor [tolerance=±5% resistance=10k package=THT]
  Q1 = PNP-Transistor [package="TO92 [THT]"]
  LED1 = LED - 5mm [color="Blue (525nm)" package="5 mm [THT]"]
  LED2 = LED - 5mm [color="Red (633nm)" package="5 mm [THT]"]
  LED3 = LED - 5mm [color="Yellow (595nm)" package="5 mm [THT]"]
  LED4 = LED - 5mm [color="Green (570nm)" package="5 mm [THT]"]
  S1 = Pushbutton [package=THT]
  U1 = mystery part, 4 pins
  R5 = Resistor [tolerance=±5% resistance=2k package=THT]

nets:
  N1: R1.Pin_0, R4.Pin_0, U1.pin4
  N2: R1.Pin_1, LED1.anode
  N3: R2.Pin_0, U1.pin3
  N4: R2.Pin_1, LED2.anode
  N5: R3.Pin_0, U1.pin2
  N6: R3.Pin_1, LED3.anode
  N7: R4.Pin_1, Q1.B, S1.leg1
  GND: Q1.E, LED2.cathode, LED3.cathode, S1.leg0
  N8: Q1.C, LED1.cathode
  N9: LED4.anode, R5.Pin_1
  N10: U1.pin1, R5.Pin_0
