# Fritzing sketch finalproject (saved by Fritzing 0.9.3b)
breadboards: 1

parts:
  V1 = DC Power [voltage=5]
  S1 = Pushbutton [package=THT]
  S2 = Pushbutton [package=THT]
  S3 = Pushbutton [package=THT]
  S4 = Pushbutton [package=THT]
  L2 = Solenoid
  L3 = Solenoid
  L1 = Solenoid
  L4 = Solenoid
  S7 = Pushbutton [package=THT]
  S6 = Pushbutton [package=THT]
  S5 = Pushbutton [package=THT]
  L5 = Solenoid
  R4 = Resistor [tolerance=±5% resistance=10k package=THT]
  R1 = Resistor [tolerance=±5% resistance=10k package=THT]
  R2 = Resistor [tolerance=±5% resistance=10k package=THT]
  R3 = Resistor [tolerance=±5% resistance=10k package=THT]
  Q1 = PNP-Transistor [package="TO92 [THT]"]
  Q2 = PNP-Transistor [package="TO92 [THT]"]
  Q3 = PNP-Transistor [package="TO92 [THT]"]
  Q4 = PNP-Transistor [package="TO92 [THT]"]
  Q5 = PNP-Transistor [package="TO92 [THT]"]
  L6 = Solenoid
  L7 = Solenoid
  L8 = Solenoid
  L9 = Solenoid
  U2 = mystery part, 2 pins
  U3 = mystery part, 2 pins
  U4 = mystery part, 2 pins
  S8 = Pushbutton [package=THT]
  U1 = mystery part, 2 pins
  R5 = Resistor [tolerance=±5% resistance=10k package=THT]
  U5 = mystery part, 1 pin

nets:
  N1: V1.V+, S1.leg0, S2.leg0, S3.leg0, S4.leg0, L5.pin1, L6.pin1, L7.pin1
  N2: V1.V-, L4.pin1, Q5.E
  N3: S1.leg1, L1.pin2
  N4: S2.leg1, L2.pin2
  N5: S3.leg1, L3.pin2
  N6: S4.leg1, L4.pin2
  GND: L2.pin1, L3.pin1, L1.pin1, R4.Pin_1, R1.Pin_1, R2.Pin_1, R3.Pin_1, Q1.E, Q2.E, Q3.E, Q4.E, R5.Pin_1
  N7: S7.leg0, U2.pin1
  N8: S7.leg1, R2.Pin_0, Q1.B, U2.pin2
  N9: S6.leg0, U3.pin1
  N10: S6.leg1, R3.Pin_0, Q3.B, U3.pin2
  N11: S5.leg0, U4.pin1
  N12: S5.leg1, R4.Pin_0, Q4.B, U4.pin2
  N13: L5.pin2, Q5.C
  N14: R1.Pin_0, Q2.B, S8.leg1, U1.pin2
  N15: Q1.C, L8.pin2
  N16: Q2.C, L9.pin2
  N17: Q3.C, L7.pin2
  N18: Q4.C, L6.pin2
  N19: Q5.B, R5.Pin_0, U5.pin1
  N20: L8.pin1, L9.pin1
  N21: S8.leg0, U1.pin1
