# Fritzing sketch circuit (saved by Fritzing 0.9.3b)
breadboards: 1

parts:
  U1 = mystery part, 2 pins [chip_label=?]
  R1 = Resistor [tolerance=±5% resistance=10k package=THT]
  M1 = DC Motor
  S1 = Pushbutton [package=THT]
  Q1 = PNP-Transistor [package="TO92 [THT]"]
  V1 = DC Power [voltage=12V]

nets:
  N1: U1.pin2, R1.Pin_1, Q1.E, V1.V-
  N2: R1.Pin_0, S1.leg1, Q1.B
  N3: M1.pin_1, V1.V+
  N4: M1.pin_2, Q1.C
