# Fritzing sketch session09 (saved by Fritzing 0.9.3b)
breadboards: 1

parts:
  U1 = mystery part, 10 pins
  J1 = Piezo Speaker
  R1 = Resistor [tolerance=±5% resistance=100 package="2512 [SMD]"]
  R2 = Resistor [tolerance=±5% resistance=100 package="2512 [SMD]"]
  R3 = Resistor [tolerance=±5% resistance=100 package="2512 [SMD]"]
  LED1 = LED - 5mm [color="Blue (470nm)" package="5 mm [THT]"]
  LED2 = LED - 5mm [color="Yellow (592nm)" package="5 mm [THT]"]
  LED3 = LED - 5mm [color="Red (633nm)" package="5 mm [THT]"]
  V1 = DC Power [voltage=12V]
  Q1 = PNP-Transistor [package="TO92 [THT]"]
  Q2 = PNP-Transistor [package="TO92 [THT]"]
  L1 = Solenoid
  L2 = Solenoid
  S1 = SWITCH-MOMENTARY-2 [package=tactile-pth]
  S2 = SWITCH-MOMENTARY-2 [package=tactile-pth]
  R4 = Resistor [tolerance=±5% resistance=10k package="2512 [SMD]"]
  R5 = Resistor [tolerance=±5% resistance=10k package="2512 [SMD]"]
  R6 = Resistor [tolerance=±5% resistance=10k package="2512 [SMD]"]
  R7 = Resistor [tolerance=±5% resistance=10k package="2512 [SMD]"]

nets:
  N1: U1.pin1, J1.pin2, LED1.cathode, LED2.cathode, LED3.cathode, V1.V-, Q1.E, Q2.E, R4.Pin_1, R5.Pin_1, R6.Pin_1, R7.Pin_1
  N2: U1.pin2, R1.Pin_0
  N3: U1.pin3, R2.Pin_0
  N4: U1.pin4, R3.Pin_0
  N5: U1.pin5, Q1.B, R5.Pin_0
  N6: U1.pin6, Q2.B, R4.Pin_0
  N7: U1.pin7, J1.pin1
  N8: U1.pin8, S2.1, R7.Pin_0
  N9: U1.pin9, S1.1, R6.Pin_0
  N10: U1.pin10, S1.2, S2.2
  N11: R1.Pin_1, LED1.anode
  N12: R2.Pin_1, LED2.anode
  N13: R3.Pin_1, LED3.anode
  N14: V1.V+, L1.pin2, L2.pin2
  N15: Q1.C, L1.pin1
  N16: Q2.C, L2.pin1
